// Logisim project au.circ as structural Verilog: 2 circuits, main circuit ALU
module ALU (
  input  [31:0] rs,
  input  [31:0] rt,
  input  [31:0] imm,
  input  [4:0] shiftAmount,
  input  [5:0] opcode,
  input  [5:0] func,
  output [31:0] result,
  output zero,
  output [1:0] PCcontrol
);

  wire BEQ, BGEZ, BGTZ, BLEZ, BNE, comparator_1_eq, comparator_1_gt, comparator_1_lt, comparator_2_lt,
       comparator_3_lt, comparator_4_eq, comparator_4_gt, comparator_6_gt, comparator_6_lt, comparator_7_eq,
       comparator_7_lt, comparator_9_eq, jmpimm, jmpreg, not_1_out, or_1_out, or_2_out;
  wire [0:0] comparator_9_lt;
  wire [2:0] branchType;
  wire [31:0] ADD, ADDi, ADDu, ADDui, AND0, ANDi, DIV, Iformat, LB, LUI, LW, MULT, NOR0, OR0, ORi, Rformat,
       SB, shifter_6_out, SLL0, SLLV0, SLT, SLTi, SRA0, SRL0, SRLV0, SUB, SUBu, SW, SYS, XOR0, XORi;

  Comparator #(.width(32)) comparator_1 (
    .a(rs), .b({32{1'b0}}), .gt(comparator_1_gt), .eq(comparator_1_eq), .lt(comparator_1_lt));
  Comparator #(.width(32)) comparator_2 (.a(rs), .b(rt), .lt(comparator_2_lt));  // open: gt, eq
  Comparator #(.width(32)) comparator_3 (.a(rs), .b(imm), .lt(comparator_3_lt));  // open: gt, eq
  Comparator #(.width(32)) comparator_4 (
    .a(rs), .b({32{1'b0}}), .gt(comparator_4_gt), .eq(comparator_4_eq));  // open: lt
  Comparator #(.width(32)) comparator_5 (.a(rs), .b(rt), .eq(BEQ));  // open: gt, lt
  Comparator #(.width(32)) comparator_6 (.a(rs), .b(rt), .gt(comparator_6_gt), .lt(comparator_6_lt));  // open: eq
  Comparator #(.width(32)) comparator_7 (
    .a(rs), .b({32{1'b0}}), .eq(comparator_7_eq), .lt(comparator_7_lt));  // open: gt
  Comparator #(.width(32)) comparator_8 (.a(rs), .b({32{1'b0}}), .gt(BGTZ));  // open: eq, lt
  or or_1 (or_1_out, comparator_1_eq, comparator_1_lt);
  or or_2 (or_2_out, comparator_1_eq, comparator_1_gt);
  Adder #(.width(32)) adder_1 (.a(rs), .b(rt), .out(ADD));  // open: cin, cout
  Subtractor #(.width(32)) subtractor_1 (.a(rs), .b(rt), .out(SUB));  // open: bin, bout
  assign XOR0 = rs ^ rt;  // XOR_Gate xor_1, 32 bits wide
  assign AND0 = rs & rt;  // AND_Gate and_1, 32 bits wide
  assign OR0 = rs | rt;  // OR_Gate or_3, 32 bits wide
  assign NOR0 = ~(rs | rt);  // NOR_Gate nor_1, 32 bits wide
  Multiplier #(.width(32)) multiplier_1 (.a(rs), .b(rt), .out(MULT));  // open: cin, cout
  Divider #(.width(32)) divider_1 (.a(rs), .b(rt), .out(DIV));  // open: upper, rem
  Shifter #(.width(32)) shifter_1 (.in(rt), .\dist (shiftAmount), .out(SLL0));
  Shifter #(.width(32)) shifter_2 (.in(rt), .\dist (rs[4:0]), .out(SLLV0));
  Shifter #(.shift("lr"), .width(32)) shifter_3 (.in(rt), .\dist (shiftAmount), .out(SRL0));
  Shifter #(.shift("lr"), .width(32)) shifter_4 (.in(rt), .\dist (rs[4:0]), .out(SRLV0));
  Shifter #(.shift("ar"), .width(32)) shifter_5 (.in(rt), .\dist (shiftAmount), .out(SRA0));
  assign SLT = {{31{1'b0}}, comparator_2_lt};  // Bit_Extender bit_extender_1
  Adder #(.width(32)) adder_2 (.a(rs), .b(imm), .out(ADDi));  // open: cin, cout
  assign SLTi = {{31{1'b0}}, comparator_3_lt};  // Bit_Extender bit_extender_2
  assign XORi = rs ^ imm;  // XOR_Gate xor_2, 32 bits wide
  assign ANDi = rs & imm;  // AND_Gate and_2, 32 bits wide
  assign ORi = rs | imm;  // OR_Gate or_4, 32 bits wide
  or or_5 (BGEZ, comparator_4_gt, comparator_4_eq);
  or or_6 (BNE, comparator_6_gt, comparator_6_lt);
  or or_7 (BLEZ, comparator_7_eq, comparator_7_lt);
  Comparator #(.width(32)) comparator_9 (.a(rs), .b(rt), .eq(comparator_9_eq), .lt(comparator_9_lt[0]));  // open: gt
  Shifter #(.width(32)) shifter_6 (.in(rt), .\dist (5'b10000), .out(shifter_6_out));
  not not_1 (not_1_out, comparator_9_eq);
  Multiplexer #(.select(3)) multiplexer_1 (
    .in1(or_2_out), .in4(comparator_9_eq), .in5(not_1_out), .in6(or_1_out), .in7(comparator_1_gt),
    .out(zero), .sel(branchType));  // open: in0, in2, in3
  Multiplexer #(.select(5), .width(32)) multiplexer_2 (
    .in0(SLL0), .in2(SRL0), .in3(SRA0), .in4(SLLV0), .in6(SRLV0), .in8(MULT), .in10(DIV), .in12(SYS),
    .in16(ADD), .in17(ADDu), .in18(SUB), .in19(SUBu), .in20(AND0), .in21(OR0), .in22(XOR0), .in23(NOR0),
    .in26(SLT), .out(Rformat), .sel({func[5], func[3:0]}));  // open: in1, in5, in7, in9, in11, in13, in14, in15, in24, in25, in27, in28, in29, in30, in31
  Multiplexer #(.select(5), .width(32)) multiplexer_3 (
    .in0(Rformat), .in8(ADDi), .in9(ADDui), .in10(SLTi), .in12(ANDi), .in13(ORi), .in14(XORi), .in15(LUI),
    .in16(LB), .in19(LW), .in24(SB), .in27(SW), .out(Iformat), .sel({opcode[5], opcode[3:0]}));  // open: in1, in2, in3, in4, in5, in6, in7, in11, in17, in18, in20, in21, in22, in23, in25, in26, in28, in29, in30, in31
  Multiplexer #(.select(5)) multiplexer_4 (
    .in1(BGEZ), .in4(BEQ), .in5(BNE), .in6(BLEZ), .in7(BGTZ), .out(jmpimm), .sel({opcode[5], opcode[3:0]}));  // open: in0, in2, in3, in8, in9, in10, in11, in12, in13, in14, in15, in16, in17, in18, in19, in20, in21, in22, in23, in24, in25, in26, in27, in28, in29, in30, in31
  Multiplexer #(.select(5)) multiplexer_5 (
    .in8(func[4]), .out(jmpreg), .sel({func[5], func[3:0]}));  // open: in0, in1, in2, in3, in4, in5, in6, in7, in9, in10, in11, in12, in13, in14, in15, in16, in17, in18, in19, in20, in21, in22, in23, in24, in25, in26, in27, in28, in29, in30, in31

  // Other names for the same wires on the sheet: OP[5:0] = opcode; PC[1:0] = PCcontrol; reg1[31:0] = rs;
  //   reg2[31:0] = rt; SA[4:0] = shiftAmount

  // Notes on the sheet:
  //   inputs
  //   outputs
  //   Comprator
  //   000100
  //   000101
  //   000110
  //   000111
  //   000001
  //   001000
  //   001111
  //   101010
  //   001010
endmodule

module ALU_Control (
  input  [31:0] reg1,
  input  [31:0] reg2,
  input  [4:0] shiftAmount,
  input  [5:0] opcode,
  input  [5:0] func,
  output [31:0] result,
  output zero,
  output [1:0] PCcontrol
);


  // Other names for the same wires on the sheet: OP[5:0] = opcode; PC[1:0] = PCcontrol; SA[4:0] = shiftAmount

  // Notes on the sheet:
  //   inputs
  //   outputs
endmodule
