// Logisim project cpu.circ as structural Verilog: 2 circuits, main circuit cpu
module cpu (
  input  in_1,
  input  in_2,
  input  in_3
);

  wire EXCLK, IDCLK, IFCLK, InstMem_p6, isJAL, isRes, isWriteRD, MEMCLK, not_1_out, syscall, WBCLK, WriteReg,
       zero;
  wire [1:0] PCcontrol;
  wire [3:0] Byte;
  wire [4:0] multiplexer_1_out, multiplexer_2_out;
  wire [25:0] ADD;
  wire [31:0] adder_2_out, DataMem_p5, imm32, multiplexer_3_out, nPC, PC4, res, rsdata, rtdata,
       shifter_1_out, writedata;
  wire [31:26] INS;

  assign imm32 = {{16{ADD[15]}}, ADD[15:0]};  // Bit_Extender bit_extender_1
  fiveCounter fivecounter_1 (
    .Start(in_1), .Clk(in_2), .miss(in_3), .S_IF(IFCLK), .S_ID(IDCLK), .S_EX(EXCLK), .S_MEM(MEMCLK),
    .S_WB(WBCLK));
  // mem InstMem: pin names not known; wires that end beside it: {INS, ADD}, 4'b0000, {32{1'b0}}, IFCLK, {INS, ADD}, InstMem_p6
  Multiplexer #(.width(5)) multiplexer_1 (.in0(ADD[20:16]), .in1(ADD[15:11]), .out(multiplexer_1_out), .sel(isWriteRD));
  Multiplexer #(.width(5)) multiplexer_2 (
    .in0(multiplexer_1_out), .in1({5{1'b1}}), .out(multiplexer_2_out), .sel(isJAL));
  Register #(.width(32)) PC (.D(nPC), .en(not_1_out), .clk(WBCLK), .Q({INS, ADD}));  // open: clr
  not not_1 (not_1_out, syscall);
  Multiplexer #(.width(32)) multiplexer_3 (.in0(writedata), .in1(PC4), .out(multiplexer_3_out), .sel(isJAL));
  Adder #(.width(32)) adder_1 (.a({INS, ADD}), .b(32'h4), .out(PC4));  // open: cin, cout
  // regfile RegisterFile: pin names not known; wires that end beside it: ADD[25:21], ADD[20:16], multiplexer_2_out, multiplexer_3_out, WriteReg, IDCLK, rsdata, rtdata
  Shifter #(.width(32)) shifter_1 (.in(imm32), .\dist (5'b00010), .out(shifter_1_out));
  Adder #(.width(32)) adder_2 (.a(PC4), .b(shifter_1_out), .out(adder_2_out));  // open: cin, cout
  Multiplexer #(.select(2), .width(32)) multiplexer_4 (
    .in0(PC4), .in1(adder_2_out), .in2(res), .in3({INS[31:28], ADD, 2'b00}), .out(nPC), .sel(PCcontrol));
  ALU alu_1 (
    .rs(rsdata), .rt(rtdata), .imm(imm32), .shiftAmount(ADD[10:6]), .opcode(INS), .func(ADD[5:0]),
    .result(res), .zero(zero), .PCcontrol(PCcontrol));  // open: SatuControll
  ALU_Control alu_control_1 (
    .reg1(rsdata), .reg2(rtdata), .shiftAmount(ADD[10:6]), .opcode(INS), .func(ADD[5:0]), .isRes(isRes),
    .isJAL(isJAL), .isWriteRD(isWriteRD), .syscall(syscall), .Byte(Byte), .WriteReg(WriteReg));
  // mem DataMem: pin names not known; wires that end beside it: res, Byte, rtdata, MEMCLK, DataMem_p5
  Multiplexer #(.width(32)) multiplexer_5 (.in0(DataMem_p5), .in1(res), .out(writedata), .sel(isRes));

  // Other names for the same wires on the sheet: func[5:0] = ADD[5:0]; imm[15:0] = ADD[15:0]; INS[25:0] = ADD;
  //   PC[31:0] = {INS, ADD}; sa[4:0] = ADD[10:6]; rd[4:0] = ADD[15:11]; rt[4:0] = ADD[20:16]; rs[4:0] = ADD[25:21];
  //   OP[5:0] = INS

  // Notes on the sheet:
  //   PC Control
endmodule

module BigBuffer (
  input  [31:0] In32_1,
  input  [31:0] In32_2,
  input  [31:0] In32_3,
  input  [31:0] In32_4,
  input  [31:0] In16_1,
  input  [31:0] In16_2,
  input  In1_1,
  input  In1_2,
  input  In1_3,
  input  In1_4,
  input  In1_5,
  input  In1_6,
  input  In1_7,
  input  In1_8,
  input  In1_9,
  input  In1_10,
  input  In1_11,
  input  In1_12,
  input  in_19,
  output [31:0] Out32_1,
  output [31:0] Out32_2,
  output [31:0] Out32_3,
  output [31:0] Out32_4,
  output [31:0] Out16_1,
  output [31:0] Out16_2,
  output Out1_1,
  output Out1_2,
  output Out1_3,
  output Out1_4,
  output Out1_5,
  output Out1_6,
  output Out1_7,
  output Out1_8,
  output Out1_9,
  output Out1_10,
  output Out1_11,
  output Out1_12
);

  Register #(.width(32)) register_1 (.D(In32_1), .clk(in_19), .Q(Out32_1));  // open: en, clr
  Register #(.width(32)) register_2 (.D(In32_2), .clk(in_19), .Q(Out32_2));  // open: en, clr
  Register #(.width(32)) register_3 (.D(In32_3), .clk(in_19), .Q(Out32_3));  // open: en, clr
  Register #(.width(32)) register_4 (.D(In32_4), .clk(in_19), .Q(Out32_4));  // open: en, clr
  Register #(.width(32)) register_5 (.D(In16_1), .clk(in_19), .Q(Out16_1));  // open: en, clr
  Register #(.width(32)) register_6 (.D(In16_2), .clk(in_19), .Q(Out16_2));  // open: en, clr
  Register #(.width(1)) register_7 (.D(In1_1), .clk(in_19), .Q(Out1_1));  // open: en, clr
  Register #(.width(1)) register_8 (.D(In1_2), .clk(in_19), .Q(Out1_2));  // open: en, clr
  Register #(.width(1)) register_9 (.D(In1_3), .clk(in_19), .Q(Out1_3));  // open: en, clr
  Register #(.width(1)) register_10 (.D(In1_4), .clk(in_19), .Q(Out1_4));  // open: en, clr
  Register #(.width(1)) register_11 (.D(In1_5), .clk(in_19), .Q(Out1_5));  // open: en, clr
  Register #(.width(1)) register_12 (.D(In1_6), .clk(in_19), .Q(Out1_6));  // open: en, clr
  Register #(.width(1)) register_13 (.D(In1_7), .clk(in_19), .Q(Out1_7));  // open: en, clr
  Register #(.width(1)) register_14 (.D(In1_8), .clk(in_19), .Q(Out1_8));  // open: en, clr
  Register #(.width(1)) register_15 (.D(In1_9), .clk(in_19), .Q(Out1_9));  // open: en, clr
  Register #(.width(1)) register_16 (.D(In1_10), .clk(in_19), .Q(Out1_10));  // open: en, clr
  Register #(.width(1)) register_17 (.D(In1_11), .clk(in_19), .Q(Out1_11));  // open: en, clr
  Register #(.width(1)) register_18 (.D(In1_12), .clk(in_19), .Q(Out1_12));  // open: en, clr

  // Other names for the same wires on the sheet: CLK = in_19
endmodule
